// Digital circuit HW1_2-bit_Multiplier.dig as structural Verilog
module HW1_2_bit_Multiplier (
  input  [1:0] A,
  input  [1:0] B,
  output [3:0] P
);

  wire and_2_out, and_3_out, and_4_out, and_5_out;

  and and_1 (P[0], A[0], B[0]);
  and and_2 (and_2_out, A[1], B[0]);
  and and_3 (and_3_out, A[0], B[1]);
  and and_4 (and_4_out, A[1], B[1]);
  and and_5 (and_5_out, and_2_out, and_3_out);
  xor xor_1 (P[1], and_2_out, and_3_out);
  and and_6 (P[3], and_4_out, and_5_out);
  xor xor_2 (P[2], and_5_out, and_4_out);
endmodule
