// Digital circuit HW1_4-bit_Full_Ripple-Carry_Adder.dig as structural Verilog
module HW1_4_bit_Full_Ripple_Carry_Adder (
  input  [3:0] A,
  input  [3:0] B,
  input  Cin,
  output [3:0] Sum,
  output Cout
);

  wire hw1_1_1_p5, hw1_1_2_p5, hw1_1_3_p5;

  // hw1_1 hw1_1_1: pin names not known; wires that end beside it: A[0], B[0], Cin, Sum[0], hw1_1_1_p5
  // hw1_1 hw1_1_2: pin names not known; wires that end beside it: A[1], B[1], hw1_1_1_p5, Sum[1], hw1_1_2_p5
  // hw1_1 hw1_1_3: pin names not known; wires that end beside it: A[2], B[2], hw1_1_2_p5, Sum[2], hw1_1_3_p5
  // hw1_1 hw1_1_4: pin names not known; wires that end beside it: A[3], B[3], hw1_1_3_p5, Sum[3], Cout
endmodule
